# Fritzing sketch product sketch (saved by Fritzing 0.9.3b)
circuit board: 7.07613cm x 5.53644cm
perfboards: 2

parts:
  Arduino_PCB = Arduino Uno (Rev3) - ICSP
  Bauteil2 = DB25F
  moisture_sensor = Infrared Proximity Sensor
  resistor_220_Ohm = Resistor [tolerance=±5% resistance=220 package=THT]
  red_soil_is_dry = LED - 5mm [color="Red (633nm)" package="5 mm [THT]"]
  green_currently_measurement = LED - 5mm [color="Green (555nm)" package="5 mm [THT]"]
  Bauteil3 = DB25M
  M1 = DC Motor
  J3 = male pin header, 1 pin [form="♂ (male)"]
  J2 = male pin header, 1 pin [form="♂ (male)"]
  J1 = male pin header, 3 pins [form="♂ (male)"]
  J4 = male pin header, 1 pin [form="♂ (male)"]
  Q1 = PNP-Transistor [package="TO92 [THT]"]
  J6 = male pin header, 1 pin [form="♂ (male)"]
  J7 = male pin header, 1 pin [form="♂ (male)"]
  J9 = male pin header, 1 pin [form="♂ (male)"]
  J8 = male pin header, 1 pin [form="♂ (male)"]
  J10 = male pin header, 1 pin [form="♂ (male)"]
  J11 = female pin header, 4 pins [form="♀ (female)"]
  J12 = female pin header, 3 pins [form="♀ (female)"]
  J13 = female pin header, 3 pins [form="♀ (female)"]
  J14 = female pin header, 2 pins [form="♀ (female)"]
  J15 = female pin header, 3 pins [form="♀ (female)"]

nets (from the breadboard view):
  N1: Arduino_PCB.A4/SDA, Bauteil2.pin3, moisture_sensor.GND, Bauteil3.pin3, J4.pin1, J14.pin1
  N2: Arduino_PCB.ICSP_MOSI, Arduino_PCB.D11_PWM/MOSI, Q1.B, J10.pin1, J13.pin3
  N3: Arduino_PCB.GND, Bauteil2.pin2, Bauteil2.pin5, Bauteil2.pin10, moisture_sensor.Vout, green_currently_measurement.cathode, Bauteil3.pin2, Bauteil3.pin5, Bauteil3.pin10, M1.pin_2, J3.pin1, J1.pin1, J1.pin2, J1.pin3, J7.pin1, J15.pin3
  N4: Arduino_PCB.D13/SCK, Bauteil2.pin9, green_currently_measurement.anode, Bauteil3.pin9, J8.pin1, J13.pin1
  N5: Arduino_PCB.D0/RX, J11.pin4
  N6: Arduino_PCB.D1/TX, J11.pin3
  N7: Arduino_PCB.D2, J11.pin2
  N8: Arduino_PCB.D3_PWM, J11.pin1
  N9: Arduino_PCB.D5_PWM, Bauteil2.pin1, moisture_sensor.Vcc, Bauteil3.pin1, J2.pin1, J12.pin3
  N10: Arduino_PCB.D7, resistor_220_Ohm.Pin_0, J12.pin1
  N11: Arduino_PCB.5V, Q1.C, J15.pin1
  N12: Bauteil2.pin4, Bauteil3.pin4, M1.pin_1, Q1.E, J6.pin1
  N13: Bauteil2.pin11, resistor_220_Ohm.Pin_1, red_soil_is_dry.anode, Bauteil3.pin11, J9.pin1
  N14: Bauteil2.pin12, red_soil_is_dry.cathode, Bauteil3.pin12

notes:
  vegetronix VH400 soil moisture sensor with
  voltage input (red)
  data output (black)
  ground (naked wire)
  http://vegetronix.com/Products/VH400/
  indicator that the soil is dry
  Power Pin D7
  vegetronix VH400 PCB wireing
  D0 = voltage input
  ground = ground
  A5 = data output / data input
  Read the moisture analog input value from the moisture sensor on A4
  indicator that currently a moisture measurement is performed
  Power Pin D13
  nanismus
  green : currently measurement
  red : soil is dry
  resistor : 220 Ohm
  moisture sensor
  Low Voltage under water pump from Barwig
  600 l/h
  voltage input
  ground
  https://www.conrad.de/de/niedervolt-tauchpumpe-barwig-0444-600-lh-6-m-539090.html
  give power to the moisture sensor
  Power Pin D5
  Indication LED
  Shows that a moisture measurement is currently performed
  PIN D13
  Indication LED
  Shows that the soil is dry
  Pin D7
  give power to the transistor to switch the 5 V power supply for the water pump
  Power Pin D11
  Transistor to switch the 5 V input for the water pump
  The digital Power I/O Pins don't provide enough current to start the pump
  RedFly Shield from watterott
  https://github.com/watterott/RedFly-Shield

// code stored in the sketch: nanismusPCB.ino
//
// nanismusPCBcode
//
// Code to run on the Arduino PCB
// Developed with [embedXcode](http://embedXcode.weebly.com)
//
// Author 		Stefan Willuda
// 				Stefan Willuda
//
// Date			01.08.16 14:31
// Version		0.66.0
//
// Copyright	© Stefan Willuda, 2016
// Licence		Creative Commons - Attribution - ShareAlike 3.0
//
// See         ReadMe.txt for references
//




// PIN Declaration ############################################################




// Declarations for status indicators LEDs


// D5
#define SoilMeasureVoltagePin 5 // Pin to start the moisture measurement


// D7
#define SoilDryWarningLED 7 // LED that indicated dryness in the soil


// D11
#define PumpVoltagePin 11 // Pin to start the waterpump to water the soil


// D13
#define CurrentlyMoistureMeasurementIndicatorLED 13 // LED that indicates that right now a moisture measurement is performed


// A4
#define MoistureMeasurementAnalogInputPin 4




// Include Libraries ###########################################################


#include <Arduino.h>




// Calculate or store constants that are uses several times in the codebase


// When we apply voltage to the moisture sensor it takes a short time for the sensor to adjust
unsigned long SoilMoistureMeasurementWaitDuration = 1000; // milliseconds 1.000 milliseconds = 1 second




// Define used variables, constants and calculations


// Every how many milliseconds are we going to perform a moisture measurement?
// currently I use millis() because I don't need the exact time and millis() is easier to simulate than now()
// 30 minutes * 60 seconds * 1000 milliseconds
unsigned long MoistMeasureInterval = 1800000; // 30 * 60 * 1000; // milliseconds 1.000 milliseconds = 1 second


// store the most recent time when the moisture measurement took place
/* When we start the first iteration of the code loop than we use the current time minus one interval
 * which leads to an immediate measurement of the soil when the board is connected to the power supply
 */
long lastMoistMeasureTime = -1 * MoistMeasureInterval;




// Define the thresholds of different analog input values to decide if they can be considered as dry, moist and so on...
/* In the Array we store different tresholds
 * position 0 --> the indicator for "urgently dry" - triggers self watering event
 * position 1 --> the indicator for "dry" - triggers the red warning lamp that asks for manual watering
 * position 2 --> the indicator for "moist" - everything is ok
 */
int MoistureIndicators[] = {0, 1, 2};


/* Store the indicator of the soil moisture
 * When we run the loop for the first time we consider the soil to be "moist";
 */
int MoistureIndicator = MoistureIndicators[2];




// Setup Start


void setup() {
    
    // Define pins and functions of these pins
    pinMode(SoilDryWarningLED, OUTPUT);  // to switch on or off the LED for dryness indication
    pinMode(SoilMeasureVoltagePin, OUTPUT); // to apply voltage to the moisture sensor
    pinMode(CurrentlyMoistureMeasurementIndicatorLED, OUTPUT); // to switch on or off the LED for measurement indication
    pinMode(PumpVoltagePin, OUTPUT);
    
    // Blink once to show that we have the new version of the code
    digitalWrite(SoilDryWarningLED, HIGH);
    delay(400);
    digitalWrite(SoilDryWarningLED, LOW);
    
}


boolean IsTimeForMoistureMeasurement() {
    
    // Check if it is time to perform a new moisture measurement
    // We don't want to measure the moisture every loop of the processor
    
    // TRUE = Yes, we need to perform a moisture measurement
    // FALSE = No, currently no new moisture measurement needed, the last moisture measurement was performed not long ago
    
    /* If the time that has passed between the last moisture measurement and now is larger than
     * the defined moisture intervall than a new moisture measurement is needed
     */
    
    unsigned long currentMillis = millis();
    if(currentMillis - lastMoistMeasureTime >= MoistMeasureInterval) {
        return(true);
    }
    else {
        return(false);
    }
}


/* Interprete the return percentage value into an LED light indication if the soil is dry
 *
 */
// Interprete the analog input from the moisture sensor
void InterpreteMoistureMeasurementAnalogInput(int Input) {
    
    // Define wether a analog input value is considered dry or moist
    // This array shall be extended later if we want a more granular distinction between dry, moist, toomoist soil
    
    // How to calculate the actual voltage input is well described at https://www.arduino.cc/en/Tutorial/ReadAnalogVoltage
    
    /* to define the thresholds for the analogInput value of the moisture sensor
     * I've measured the voltage input in a glass of water, which I consider to be wet and it was 0.7 volts input
     * Considering the formular: voltage= sensorValue * (5.0 / 1023.0)
     * I've measured different states of moisture to collect example data
     * If the moisture sensor sticks in a glass of water I can measure with a multimeter 2.6 Volts input
     *		100% moist = 2.6 V = 532 analogInput
     * If the moisture sensor sticks to really dry soil = 10% wet = 1,0 V
     *      10% moist = 1,00 V = 205 analogInput
     * If the moisture sensor sticks in soil that is considered 40% wet = 1,66 V
     *		40% moist = 1,66 V = 340 analogInput
     * If the moisture sensor sticks in soil that has been watered right now = 2,16 V
     *		80% moist = 2,16 V = 442 analogInput
     * If the moisture sensor sticks in soil that is still water wet after a watering = 2,35 V
     *		90% moist = 2,35 V = 481 analogInput
     * I can assume that 100 analogInput indicates wet soil
     */
    
    // "urgently dry", "dry"
    int ThresholdsForAnalogInputValues[] = {260, 340};
    
    // Check if the analog input value from the moisture sensor is considered to indicate an "urgently dry" soil
    if(Input <= ThresholdsForAnalogInputValues[MoistureIndicators[0]]){
        
        // retun that the soil is considered "urently dry"
        MoistureIndicator = MoistureIndicators[0];
        
    }
    // Check if the analog input value from the moisture sensor is considered to indicate a "dry" soil
    else if(Input <= ThresholdsForAnalogInputValues[MoistureIndicators[1]]){
        
        // retun that the soil is considered "dry"
        MoistureIndicator = MoistureIndicators[1];
        
    }
    else {
        
        // return that the soil is considred "moist"
        MoistureIndicator = MoistureIndicators[2];
    }
}




// Start the actual moisture measurement by calling data from the moisture sensor
void PerformMoistureMeasurement(){
    
    // idicate with an LED that a measurement is currently performed
    digitalWrite(CurrentlyMoistureMeasurementIndicatorLED, HIGH);
    
    // apply voltage to soil moisture sensor
    digitalWrite(SoilMeasureVoltagePin, HIGH);
    
    /* wait for a short time that the soil moisture sensor can adjust
     * I know, that I could have used delay() but for some reasons I encounterd
     * timing problems with delays longer than 900 ms
     */
    // Therefore store the current time
    unsigned long currentMillis = millis();
    
    // store the beginning of this measurement
    unsigned long firstMeasureTime = currentMillis;
    
    // Go through a loop until the duration it takes to perform a moisture measurement is over
    while (currentMillis - firstMeasureTime < SoilMoistureMeasurementWaitDuration) {
        
        currentMillis = millis();
    }
    
    // collect the data input that is sent by the soil moisture sensor and store it for reuseage
    int MoistureMeasurementResultAnalogInput = analogRead(MoistureMeasurementAnalogInputPin);
    
    // switch of the voltage of the moisture sensor
    digitalWrite(SoilMeasureVoltagePin, LOW);
    
    // switch off the indication LED
    digitalWrite(CurrentlyMoistureMeasurementIndicatorLED, LOW);
    
    // Interprete the analog input value from the sensor
    InterpreteMoistureMeasurementAnalogInput(MoistureMeasurementResultAnalogInput);
}




/* Measure the moisture of the soil
 * but only if it is already time to do the measurement
 */
void MoistureMeasurement(boolean IsTimeForMoistureMeasurement) {
    
    // is it already time to perform a new moisture check?
    if(IsTimeForMoistureMeasurement) {
        
        /* Store the current time to "remember" when the last moisture measurement took place
         * This information will be needed to decide in later loops of the code if it is time
         * to perform a new measurement
         */
        lastMoistMeasureTime = millis();
        
        // Start the measurement of the current soil moisture
        PerformMoistureMeasurement();
    }
}




// Decide if we need to switch the Dryness Warning LED on or off based on the interpretation of the moisture sensor analog input
void DecisionToSwitchSoilDryWaringLED(int Indicator){


    // remember the moisture indicator in this switch statement if "0" some day no longer means "urgently dry"
    // and "1" does no longer mean "dry"
    // MoistureIndicators[0];
    
    switch(Indicator){ // What kind of soil moisture indicator did we receive?
            
        case 0: // the soil is urgently dry
        case 1: // the soil is dry
            
            // switch on the red dryness indication LED
            digitalWrite(SoilDryWarningLED, HIGH);
            break;
            
        default: // in all the cases where the soil is not "dry" or "urgently dry" no warning LED is needed
            
            // switch of the red dryness indication LED
            digitalWrite(SoilDryWarningLED, LOW);
            break;
    }
}




// Switch on the water pump by switching the transistor
void StartTheWaterPump(){
    
    /* store when the pump action started
     * check how long the self watering action is currently performed
     * check if the soil is already "moist" again
     * stop the watering immediately if the time for the watering is up or the soil is "moist" again to avoid water overflow
     */
    
    unsigned long CurrentMillis = millis(); // recurring check of the current time
    unsigned long PumpBeginningMillis = CurrentMillis; // this value serves to compare start and end time of the watering action
    unsigned long PumpDurationMillis = 10000; // water for 10 seconds. This provides 300 ml of water
    
    while ((CurrentMillis - PumpBeginningMillis < PumpDurationMillis) && (MoistureIndicator != MoistureIndicators[2])) {
        
        // switch on the water pump
        digitalWrite(PumpVoltagePin, HIGH);
        
        // check if the soil is "moist" already;
        PerformMoistureMeasurement();
        
        CurrentMillis = millis();
    }
    
    // stop the water pump
    digitalWrite(PumpVoltagePin, LOW);
}




// Decide if we need to switch on the water pump to perform a self watering action based on the interpretation of the moisture sensor analog input
void DecisionToSwitchWaterPump(int Indicator){
    
    // remember the moisture indicator in this switch statement if "0" some day no longer means "urgently dry"
    // MoistureIndicators[0];
    
    switch (Indicator) {
        case 0: // the soil is "urgently dry"
            
            // start the self watering action
            StartTheWaterPump();
            
            break;
            
        default:
            // do nothing but ensure that there is no power supply to the transistor
            digitalWrite(PumpVoltagePin, LOW);
            
            break;
    }
}


void loop() {
    
    /* Check if it is time to start the measurement of the soil moisture
     * The return of this check is a simple TRUE or FALSE statement
     * We use this statement to pass it on to following functions to decide e.g. if a moisture
     * needs to take place
     */
    
    /* Start the moisture measurement
     * Cosider the TRUE or FALSE statement from the time check before
     * The return of this moisture measurement is an analog input value
     * This analog input value is then converted into a percentage value in three ranges which lead to an interpretation
     * of the current moisture status of the soil - let's start with green, yellow, red
     */
    MoistureMeasurement(IsTimeForMoistureMeasurement());
    
    /* Decide if the red dryness warning indication LED needs to be swiched on or off based on the moisture
     * interpretation
     */
    DecisionToSwitchSoilDryWaringLED(MoistureIndicator);
    
    /* Decide if the water pump to water the soil automatically should be switched on
     * This decision will be based on the last moisture measurement of the moisture sensor
     * If the soil is "urgently dry" the waterpump will immediately start watering the soil
     */
    DecisionToSwitchWaterPump(MoistureIndicator);
    
}
